# Fritzing sketch SMS commander (saved by Fritzing 0.9.4)

parts:
  U1 = V_REG_LD1117VXX [package=78xxl]
  R1 = Resistor [tolerance=±5% resistance=1k package=THT]
  Plain_Vanilla_ESP3 = Plain Vanilla ESP32
  R14 = Resistor [tolerance=±10% resistance=15k package=THT]
  R15 = Resistor [tolerance=±10% resistance=15k package=THT]
  J3 = single row smd male pin header, 6 pins [form="♂ (male)" part_number="To the programmer"]
  J4 = single row smd male pin header, 2 pins [form="♂ (male)"]  # not connected
  M1 = MT3608 Module
  M2 = TP4056 Module [part_number=HW-107]
  C3 = Capacitor Polarized [part_number="4.700 uF" package=nippon_f80]
  BAT1 = Battery Holders [package=lipo-1100mAh]
  HC-SR04_Sensor_1 = HC-SR04 Ultrasonic Distance Sensor
  SIM800L1 = SIM800L
  KF-1 = KF-301 Relay [package=THT]
  S1 = SPST Switch [package=switch-spdt-smd]
  HLK-PM1 = HLK-PM01
  C4 = Capacitor Polarized [part_number="10 uF" package=nippon_f80]
  JP1 = Header 4 [package=molex-1x4_lock]

nets:
  N1: U1.OUT, Plain_Vanilla_ESP3.SVN, Plain_Vanilla_ESP3.IO16, Plain_Vanilla_ESP3.3.3V, R14.Pin_1, R15.Pin_1, C4.+
  GND: U1.GND, Plain_Vanilla_ESP3.GND, J3.pin2, M1.pin4, C3.-, HC-SR04_Sensor_1.GND, SIM800L1.GND, KF-1.ground, S1.P, C4.-, JP1.1
  VCC: U1.IN, M1.pin3, C3.+, HC-SR04_Sensor_1.VCC, SIM800L1.VCC, KF-1.power, JP1.4
  N2: R1.Pin_0, S1.S
  N3: R1.Pin_1, Plain_Vanilla_ESP3.IO33
  N4: Plain_Vanilla_ESP3.IO26, KF-1.signal
  N5: Plain_Vanilla_ESP3.IO13, HC-SR04_Sensor_1.TRIG, JP1.3
  N6: Plain_Vanilla_ESP3.IO27, HC-SR04_Sensor_1.ECHO, JP1.2
  N7: Plain_Vanilla_ESP3.EN, R15.Pin_0, J3.pin5
  N8: Plain_Vanilla_ESP3.IO0, R14.Pin_0, J3.pin6
  N9: Plain_Vanilla_ESP3.TXD, J3.pin4
  N10: Plain_Vanilla_ESP3.RXD, J3.pin3
  N11: Plain_Vanilla_ESP3.IO21, SIM800L1.RST
  N12: Plain_Vanilla_ESP3.IO18, SIM800L1.TXD
  N13: Plain_Vanilla_ESP3.IO17, SIM800L1.RXD
  N14: M1.pin1, M2.pin2
  N15: M2.pin1, HLK-PM1.+Vo
  N16: M2.pin3, BAT1.-
  N17: M2.pin4, BAT1.+
  N18: M2.pin6, HLK-PM1.-Vo

notes:
  FTDI programmer connector
  VCC
  GND
  RXD < -------- TXD
  TXD -----------> RXD
  EN/RST
  IO0/FLASH
  VCC: 4.5V
  GND
  SIM800L pinout
  VCC
  RST (active LOW)
  RXD SIM
  TXD
  GND
  Input
  NC or NO
  Output
  LED
  YELLOW: input ON (closed contact)
  3.3V
  LEDs
  RED: battery on charge
  BLUE: battery charged
  RED LED
  blinking every second: no GSM signal.
  Blinking every 3 seconds: GSM signal OK
  Distance
  5-400 cm

custom parts:
  MT3608 Module: MT3608 Boost Converter Module Links: Aerosemi MT3608 2A Step Up Converter datasheet
  TP4056 Module: TP4056 Lithium Battery Charge Management Module Links: TP4056 website
  SIM800L: SIM800L is a miniature cellular module which allows for GPRS transmission, sending and receiving SMS and making and receiving voice calls. Low cost and small footprint and quad band frequency support make this module perfect solution for any project that require long range connectivity. After connecting power module boots up, searches for cellular network and login automatically. On board LED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
  KF-301 Relay: KF-301
